# Fritzing sketch Circuit (saved by Fritzing 0.9.3b)
breadboards: 1

parts:
  D1 = SOLAR-IXYS [package=solarbit-12x1]
  D2 = SOLAR-IXYS [package=solarbit-12x1]
  D3 = SOLAR-IXYS [package=solarbit-12x1]
  C1_1F = Capacitor Polarized [package=cpol-radial-1000uf-25v]
  J1 = Basic Servo
  M1 = DC Motor
  U4 = RELAY [package=relay-jzc]
  C2_5F = Capacitor Polarized [package=cpol-radial-1000uf-25v]
  3_3V = Voltage Regulator - 3.3V [package="TO220 [THT]"]
  C1_0_1μF = Ceramic Capacitor [capacitance=100nF package="100 mil [THT, multilayer]"]
  C1_47μF = Electrolytic Capacitor [capacitance=1µF package="100 mil [THT, electrolytic]"]
  U5 = ESP-WROOM-02 WiFi MCU module [part_number=ESP-WROOM-02]
  R1_10k = Resistor [tolerance=±5% resistance=220 package=THT]
  R2 = Resistor [tolerance=±5% resistance=220 package=THT]
  R3 = Resistor [tolerance=±5% resistance=220 package=THT]
  R5 = Resistor [tolerance=±5% resistance=220 package=THT]
  U2 = RELAY [package=relay-jzc]
  LED1 = smd LED [color="Red (633nm)" package="0603 [SMD]"]
  LED2 = smd LED [color="Red (633nm)" package="0603 [SMD]"]
  R6 = Resistor [tolerance=±5% resistance=220 package=THT]

nets:
  N1: D1.A, D2.A, U4.MAIN, U4.COIL1, C2_5F.-, 3_3V.GND, C1_0_1μF.0, C1_47μF.-, U5.9_GND, U5.13_GND, U5.18_GND, R3.Pin_0, U2.COIL2, R6.Pin_0
  N2: D1.C, D2.C, M1.pin_1, C2_5F.+, 3_3V.input_voltage, U2.NC
  N3: D3.A, C1_1F.-, J1.gnd
  N4: D3.C, C1_1F.+, U2.MAIN
  N5: J1.vcc, U2.NO
  N6: J1.pulse, U5.3_IO14
  N7: M1.pin_2, U4.NO
  N8: U4.COIL2, U5.10_IO4
  N9: 3_3V.output_voltage, C1_0_1μF.1, C1_47μF.+, R1_10k.Pin_0, R2.Pin_0, R5.Pin_0, LED1.anode
  N10: U5.1_3V3, LED1.cathode
  N11: U5.2_EN, R1_10k.Pin_1
  N12: U5.6_IO15, R3.Pin_1
  N13: U5.7_IO2, R5.Pin_1
  N14: U5.8_IO0, R2.Pin_1
  N15: U5.11_IO3/RXD, U2.COIL1
  N16: U5.14_IO5, LED2.anode
  N17: LED2.cathode, R6.Pin_1

custom parts:
  ESP-WROOM-02 WiFi MCU module: ESP-WROOM-02 by espressif, Well supported Arduino libraries are available.
